# Fritzing sketch jenga_1117 (saved by Fritzing 0.9.3b)
circuit board: 2.6cm x 7.9cm
breadboards: 1

parts:
  C5 = Ceramic Capacitor [capacitance=4.7µF package="100 mil [THT, multilayer]"]
  C6 = Ceramic Capacitor [capacitance=4.7µF package="100 mil [THT, multilayer]"]
  Battery1 = Header 2 [package=jst-2-pth]
  C7 = Ceramic Capacitor [capacitance=0.1µF voltage=20V package="100 mil [THT, multilayer]"]
  Atmega1 = ATmega328 [package=tqfp]
  MCP73831 = MCP73831 [package=sot23-5]
  USB1 = USB Connectors [package=usb-microb]
  led = smd LED [color="Red (633nm)" package="0805 [SMD]"]
  R5 = Resistor [tolerance=±5% resistance=2.2k package="0805 [SMD]"]
  R1 = Resistor [tolerance=±5% resistance=330 package="0805 [SMD]"]
  writer = female pin header, 6 pins [form="♀ (female)"]
  neo4 = ws2812b [package="smd 2812b"]
  neo3 = ws2812b [package="smd 2812b"]
  neo1 = ws2812b [package="smd 2812b"]
  neo2 = ws2812b [package="smd 2812b"]
  kxsc7-2050 = IC, DIP package, 8 pins [chip_label=IC]

nets:
  GND: C5.0, C6.0, Battery1.1, C7.0, Atmega1.GND, MCP73831.VSS, USB1.GND, R5.Pin_0, writer.pin2, neo4.VSS, neo3.VSS, neo1.VSS, neo2.VSS, kxsc7-2050.pin4
  3.7V/led power: C5.1, Battery1.2, C7.1, Atmega1.VCC, Atmega1.PB1(OC1A), Atmega1.AVCC, MCP73831.VBAT, writer.pin1, neo4.VDD, neo3.VDD, neo1.VDD, neo2.VDD
  N1: C6.1, MCP73831.VIN, USB1.VBUS, led.anode
  acc p: Atmega1.PD3(INT1), kxsc7-2050.pin5, kxsc7-2050.pin6, kxsc7-2050.pin8
  LED PIN: Atmega1.PD6(AIN0), neo1.DIN
  N2: Atmega1.PB3(MOSI_OC2), writer.pin4
  N3: Atmega1.PB4(MISO), writer.pin5
  N4: Atmega1.PB5(SCK), writer.pin6
  X: Atmega1.PC0(ADC0), kxsc7-2050.pin1
  Y: Atmega1.PC1(ADC1), kxsc7-2050.pin2
  Z: Atmega1.PC2(ADC2), kxsc7-2050.pin3
  N5: Atmega1.PC6(_RESET), writer.pin3
  N6: MCP73831.STAT, R1.Pin_0
  N7: MCP73831.PROG, R5.Pin_1
  N8: led.cathode, R1.Pin_1
  N9: neo4.DIN, neo3.DOUT
  N10: neo3.DIN, neo2.DOUT
  N11: neo1.DOUT, neo2.DIN

notes:
  xyzg
  gnd
  sck
  miso
  mosi
  reset
  VCC
